# Fritzing sketch Reptile Habitat Shield (saved by Fritzing 0.7.12b)
breadboards: 1

parts:
  Arduino = Arduino
  Q1 = NPN-Transistor [package="TO92 [THT]"]
  Q2 = NPN-Transistor [package="TO92 [THT]"]
  Q3 = NPN-Transistor [package="TO92 [THT]"]
  R1 = Resistor [tolerance=±5% resistance=220 package=THT]
  R2 = Resistor [tolerance=±5% resistance=220 package=THT]
  R3 = Resistor [tolerance=±5% resistance=220 package=THT]
  V1 = shrouded pin header, 10 pins [form="♂ (shrouded male)"]
  R6 = Resistor [tolerance=±5% resistance=10k package=THT]
  R5 = Resistor [tolerance=±5% resistance=10k package=THT]
  R4 = Resistor [tolerance=±5% resistance=220 package=THT]
  D1 = Rectifier Diode [part_number=1N4001 package="300 mil [THT]"]
  R7 = Resistor [tolerance=±5% resistance=10k package=THT]
  R8 = Resistor [tolerance=±5% resistance=10k package=THT]
  V2 = shrouded pin header, 10 pins [form="♂ (shrouded male)"]
  Relays = Generic male header - 6 pins [package=THT]
  RTC = Generic male header - 5 pins [package=THT]
  Q4 = NPN-Transistor [package="TO92 [THT]"]
  LCD = shrouded pin header, 14 pins [form="♂ (shrouded male)"]
  Pot = Rotary Potentiometer (Small) [maximum_resistance=100kΩ]

nets:
  N1: Arduino.aref, Arduino.3V3, R6.Pin_1, R5.Pin_1, R7.Pin_1, R8.Pin_1
  N2: Arduino.GND, Q1.E, Q2.E, Q3.E, V1.pin9, V1.pin10, V2.pin9, V2.pin10, Relays.pin6, RTC.pin1, Q4.E, LCD.pin1, LCD.pin3, LCD.pin8, Pot.leg2
  N3: Arduino.D13, LCD.pin9
  N4: Arduino.D12, Relays.pin2
  N5: Arduino.D11, Relays.pin3
  N6: Arduino.D10, Relays.pin4
  N7: Arduino.D9, R4.Pin_1
  N8: Arduino.D8, Relays.pin5
  N9: Arduino.D7, LCD.pin6
  N10: Arduino.D6, R3.Pin_1
  N11: Arduino.D5, R2.Pin_1
  N12: Arduino.D4, LCD.pin10
  N13: Arduino.D3, R1.Pin_1
  N14: Arduino.D2, LCD.pin5
  N15: Arduino.D1TX, LCD.pin12
  N16: Arduino.D0RX, LCD.pin13
  N17: Arduino.+5V, Relays.pin1, RTC.pin2, LCD.pin7, LCD.pin14, Pot.leg1
  N18: Arduino.VIN, V1.pin4, V1.pin6, D1.cathode, V2.pin4, V2.pin6
  N19: Arduino.A0, V1.pin1, R5.Pin_0
  N20: Arduino.A1, V1.pin2, R6.Pin_0
  N21: Arduino.A2, R7.Pin_0, V2.pin1
  N22: Arduino.A3, R8.Pin_0, V2.pin2
  N23: Arduino.A4, RTC.pin3
  N24: Arduino.A5, RTC.pin4
  N25: Q1.B, R1.Pin_0
  N26: Q1.C, V1.pin7, V2.pin7
  N27: Q2.B, R2.Pin_0
  N28: Q2.C, V1.pin8, V2.pin8
  N29: Q3.B, R3.Pin_0
  N30: Q3.C, V1.pin3, V2.pin3
  N31: V1.pin5, D1.anode, V2.pin5, Q4.C
  N32: R4.Pin_0, Q4.B
  N33: LCD.pin2, Pot.wiper

notes:
  Habitat Control Shield
  SPATTE88 @ RFUK
  V1.0
